# Fritzing sketch Arfuino_Backend (saved by Fritzing 0.9.3b)
breadboards: 1

parts:
  Bauteil1 = Arduino Uno (Rev3)
  R1 = Rotary Potentiometer (Small) [maximum_resistance=100kΩ package=THT]
  R2 = Rotary Potentiometer (Small) [maximum_resistance=100kΩ package=THT]
  R4 = Rotary Potentiometer (Small) [maximum_resistance=100kΩ package=THT]
  J4 = Basic Servo
  S1 = Pushbutton [package="[THT]"]
  S2 = Pushbutton [package="[THT]"]
  R3 = Rotary Potentiometer (Small) [maximum_resistance=100kΩ package=THT]
  J5 = Basic Servo
  J6 = Basic Servo
  J7 = Basic Servo
  R5 = Resistor [tolerance=±5% resistance=220 package=THT]
  R6 = Resistor [tolerance=±5% resistance=220 package=THT]

nets:
  N1: Bauteil1.A1, R4.wiper
  N2: Bauteil1.A2, R2.wiper
  N3: Bauteil1.A3, R1.wiper
  N4: Bauteil1.D8, S2.Pin_1, S2.Pin_2, R6.Pin_0
  N5: Bauteil1.D9_PWM, S1.Pin_1, S1.Pin_2, R5.Pin_0
  GND: Bauteil1.GND, R1.leg1, R2.leg1, R4.leg1, J4.gnd, R3.leg1, J5.gnd, J6.gnd, J7.gnd, R5.Pin_1, R6.Pin_1
  N6: Bauteil1.D2, J7.pulse
  N7: Bauteil1.D3_PWM, J6.pulse
  N8: Bauteil1.D4, J5.pulse
  N9: Bauteil1.D5_PWM, J4.pulse
  VCC: Bauteil1.5V, R1.leg2, R2.leg2, R4.leg2, J4.vcc, S1.Pin_4, S2.Pin_3, S2.Pin_4, R3.leg2, J5.vcc, J6.vcc, J7.vcc
